# Fritzing sketch 12v (saved by Fritzing 0.9.3b)
circuit board: 2.95024cm x 1.73437cm
perfboards: 1

parts:
  7805 = 7805 Low-Dropout Voltage Regulator
  R1 = Resistor [tolerance=±5% resistance=220 package=THT]
  C1 = Capacitor Polarized [package=eia3528]
  C2 = Capacitor Polarized [package=eia3528]
  C4 = Capacitor Polarized [package=eia3528]
  LED1 = LED - 5mm [color="Red (633nm)" package="5 mm [THT]"]
  J1 = female pin header, 2 pins [form="♀ (female)"]
  J2 = female pin header, 2 pins [form="♀ (female)"]
  C3 = Capacitor Polarized [package=eia3528]

nets:
  GND: 7805.GND, 7805.Vin, C1.+, C1.-, C2.+, C2.-, C4.-, LED1.anode, J1.pin1, J1.pin2, J2.pin2, C3.-
  N1: 7805.Vout, R1.Pin_0, C4.+, J2.pin1, C3.+
  N2: R1.Pin_1, LED1.cathode
